# Fritzing sketch ServoModule (saved by Fritzing 1.0.2b)
circuit board: 4.3491cm x 8.93052cm
breadboards: 1

parts:
  C1 = Electrolytic Capacitor [capacitance=1µF voltage=35V package="100 mil [THT, electrolytic]"]
  C2 = Electrolytic Capacitor [capacitance=1µF voltage=35V package="100 mil [THT, electrolytic]"]
  C3 = Electrolytic Capacitor [capacitance=1µF voltage=35V package="100 mil [THT, electrolytic]"]
  VIN = Screw terminal - 2 pins [package=THT]
  D2 = Rectifier Diode [part_number=1N4001 package="300 mil [THT]"]
  JP1 = FTDI_BASIC [package=ftdi_basic]
  JP2 = FTDI_BASIC [package=ftdi_basic]
  JP3 = FTDI_BASIC [package=ftdi_basic]
  GND = FTDI_BASIC [package=ftdi_basic]
  V = FTDI_BASIC [package=ftdi_basic]
  C4 = Electrolytic Capacitor [capacitance=1µF voltage=35V package="100 mil [THT, electrolytic]"]
  C5 = Electrolytic Capacitor [capacitance=1µF voltage=35V package="100 mil [THT, electrolytic]"]
  C6 = Electrolytic Capacitor [capacitance=1µF voltage=35V package="100 mil [THT, electrolytic]"]
  SIGNAL_IN = FTDI_BASIC [package=ftdi_basic]
  Fuse1 = Fuse with Handler [part_number=Htc-15m]
  D1 = Rectifier Diode [part_number=1N4001 package="300 mil [THT]"]
  ARDUINO_OUT = Screw terminal - 2 pins [package=THT]
  C7 = Capacitor [package=cap-pth-small2]
  C8 = Capacitor [package=cap-pth-small2]
  C9 = Capacitor [package=cap-pth-small2]
  C10 = Capacitor [package=cap-pth-small2]
  C11 = Capacitor [package=cap-pth-small2]
  C12 = Capacitor [package=cap-pth-small2]

nets:
  N1: C1.-, C2.-, C3.-, VIN.pin1, JP1.6, JP1.3, JP2.6, JP2.3, JP3.6, JP3.3, GND.5, GND.1, GND.6, GND.2, GND.3, GND.4, C4.-, C5.-, C6.-, ARDUINO_OUT.pin1, C7.2, C8.2, C9.2, C10.2, C11.2, C12.2
  N2: C1.+, C2.+, C3.+, D2.cathode, JP1.5, JP1.2, JP2.5, JP2.2, JP3.5, JP3.2, C4.+, C5.+, C6.+, C7.1, C8.1, C9.1, C11.1, C12.1
  N3: VIN.pin2, Fuse1.Connector1
  N4: D2.anode, D1.cathode, ARDUINO_OUT.pin2
  N5: JP1.1, SIGNAL_IN.5
  N6: JP1.4, SIGNAL_IN.6
  N7: JP2.1, SIGNAL_IN.3
  N8: JP2.4, SIGNAL_IN.4
  N9: JP3.1, SIGNAL_IN.1
  N10: JP3.4, SIGNAL_IN.2
  N11: V.5, V.1, V.6, V.2, V.3, V.4
  N12: Fuse1.Connector2, D1.anode

notes:
  THS-DEVS
  Servo Module v1.0
  +
  -
